# Fritzing sketch main (saved by Fritzing 1.0.2b)
breadboards: 1

parts:
  Left_Wheel_Motor = DC Motor [voltage_(max)=6V voltage_(min)=3V]  # not connected
  Right_Wheel_Motor = DC Motor [voltage_(max)=6V voltage_(min)=3V]  # not connected
  Mod1 = L298N DC motor driver
  3S_LiPo_12V_Battery = Battery block 9V
  Part2 = InvenSense MPU6050
  Part1 = Arduino Nano (Rev3.0)

nets:
  5V: Mod1.5V, Mod1.+5V-J2, Part1.VIN
  N1: Mod1.ENA, Part1.D6
  N2: Mod1.IN1, Part1.D10
  N3: Mod1.IN2, Part1.D9
  N4: Mod1.IN3, Part1.D8
  N5: Mod1.IN4, Part1.D7
  N6: Mod1.ENB, Part1.D5
  GND: 3S_LiPo_12V_Battery.-, Part2.GND, Part1.GND
  VCC: Part2.VCC, Part1.5V, Part1.A7
  N7: Part2.SCL, Part1.A6, Part1.A5
  N8: Part2.SDA, Part1.A4
  N9: Part2.INT, Part1.D4

custom parts:
  L298N DC motor driver: 2x DC motor driver with 78M05 positive voltage regulator (7..35 V) L298N: max 46 V, 2 A Set 5 V Enable jumper to enable 5 V regultor (needed for the L298N) and +5 V output at screw terminal or supply external +5 V at screw terminal Set ENA and/or ENB to +5 V to enable motor permanently or supply ENA and/or ENB with PWM signal IN1 and IN2 set rotation directory for motor A (OUT1/OUT2) IN2 and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
  Battery block 9V: Your standard 9 Volts battery block
