# Fritzing sketch nanol298ntest (saved by Fritzing 1.0.2b)
breadboards: 1

parts:
  Part1 = Arduino Nano (Rev3.0)
  Mod1 = L298N DC motor driver
  VCC1 = Battery block 9V
  right_motor = DC Motor [voltage_(max)=6V voltage_(min)=3V]  # not connected
  left_motor = DC Motor [voltage_(max)=6V voltage_(min)=3V]  # not connected

nets:
  GND: Part1.GND, Mod1.GND, VCC1.-
  N1: Part1.D5, Mod1.ENB
  N2: Part1.D6, Mod1.ENA
  N3: Part1.D7, Mod1.IN4
  N4: Part1.D8, Mod1.IN3
  N5: Part1.D9, Mod1.IN2
  N6: Part1.D10, Mod1.IN1
  VIN: Part1.VIN, Mod1.5V

custom parts:
  L298N DC motor driver: 2x DC motor driver with 78M05 positive voltage regulator (7..35 V) L298N: max 46 V, 2 A Set 5 V Enable jumper to enable 5 V regultor (needed for the L298N) and +5 V output at screw terminal or supply external +5 V at screw terminal Set ENA and/or ENB to +5 V to enable motor permanently or supply ENA and/or ENB with PWM signal IN1 and IN2 set rotation directory for motor A (OUT1/OUT2) IN2 and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
  Battery block 9V: Your standard 9 Volts battery block
