# Fritzing sketch nanomputest (saved by Fritzing 1.0.2b)
breadboards: 1

parts:
  Part1 = Arduino Nano (Rev3.0)
  Part2 = InvenSense MPU6050

nets:
  GND: Part1.GND, Part2.GND
  5V: Part1.5V, Part2.VCC
  N1: Part1.A5, Part2.SCL
  N2: Part1.A4, Part2.SDA
